// Logisim project auto_arm_proj.circ as structural Verilog: 6 circuits, main circuit auto_arm_simulation
module auto_arm_simulation (
);

  wire auto_arm_top_1_dest_blue_o, auto_arm_top_1_dest_init_o, auto_arm_top_1_dest_red_o,
       auto_arm_top_1_drop_o, auto_arm_top_1_move_o, auto_arm_top_1_scan_o, auto_arm_top_1_throw_o,
       clk_i_out, tclconsolereds_1_p23, tclconsolereds_1_p26;
  wire [1:0] tclconsolereds_1_p24;

  Clock clk_i (.out(clk_i_out));
  Clock sysclk ();  // open: out
  auto_arm_top auto_arm_top_1 (
    .ready_i(tclconsolereds_1_p23), .color_i(tclconsolereds_1_p24), .clk_i(clk_i_out),
    .reset_i(tclconsolereds_1_p26), .scan_o(auto_arm_top_1_scan_o), .throw_o(auto_arm_top_1_throw_o),
    .move_o(auto_arm_top_1_move_o), .dest_red_o(auto_arm_top_1_dest_red_o),
    .dest_blue_o(auto_arm_top_1_dest_blue_o), .dest_init_o(auto_arm_top_1_dest_init_o),
    .drop_o(auto_arm_top_1_drop_o));
  // TclConsoleReds #(.filePath("console/console_auto_arm.tcl")) tclconsolereds_1: pin names not known; wires that end beside it: 4'b0000, 4'b0000, auto_arm_top_1_scan_o, auto_arm_top_1_throw_o, auto_arm_top_1_move_o, auto_arm_top_1_dest_red_o, auto_arm_top_1_dest_blue_o, auto_arm_top_1_dest_init_o, auto_arm_top_1_drop_o, 1'b0, 1'b0, 1'b0, 1'b0, 1'b0, 1'b0, 1'b0, 1'b0, 1'b0, {16{1'b0}}, {16{1'b0}}, {8{1'b0}}, clk_i_out, tclconsolereds_1_p23, tclconsolereds_1_p24[0], tclconsolereds_1_p24[1], tclconsolereds_1_p26

  // Notes on the sheet:
  //   Attention, votre version de Logisim
  //   ne contient pas de tracker. Si vous
  //   enregistrez votre projet, toutes les
  //   informations du tracker seront
  //   définitivement effacées.
endmodule

module auto_arm_top (
  input  ready_i,
  input  [1:0] color_i,
  input  clk_i,
  input  reset_i,
  output scan_o,
  output throw_o,
  output move_o,
  output dest_red_o,
  output dest_blue_o,
  output dest_init_o,
  output drop_o
);

  wire [6:0] decodeur_etats_futurs_1_etat_futur, registre_7_bits_1_out_o;

  decodeur_etats_futurs decodeur_etats_futurs_1 (
    .etat_actuel(registre_7_bits_1_out_o), .ready_i(ready_i), .color_i(color_i), .clk_i(clk_i),
    .etat_futur(decodeur_etats_futurs_1_etat_futur));
  registre_7_bits registre_7_bits_1 (
    .in_i(decodeur_etats_futurs_1_etat_futur), .reset_i(reset_i), .clk(clk_i), .out_o(registre_7_bits_1_out_o));
  decodeur_sorties decodeur_sorties_1 (
    .in_i(registre_7_bits_1_out_o),
    .out_o({drop_o, dest_init_o, dest_blue_o, dest_red_o, move_o, throw_o, scan_o}));

  // Notes on the sheet:
  //   Attention, votre version de Logisim
  //   ne contient pas de tracker. Si vous
  //   enregistrez votre projet, toutes les
  //   informations du tracker seront
  //   définitivement effacées.
endmodule

module timer (
  input  load_i,
  input  enable_i,
  input  clk_i,
  input  reset_i,
  output out_o
);

  wire [1:0] multiplexer_1_out, register_1_q, subtractor_1_out;

  Subtractor #(.width(2)) subtractor_1 (.a(register_1_q), .b(2'b01), .out(subtractor_1_out), .bin(1'b0));  // open: bout
  Multiplexer #(.width(2), .enable("false")) multiplexer_1 (
    .in0(subtractor_1_out), .in1(2'b11), .out(multiplexer_1_out), .sel(load_i));
  Register #(.width(2)) register_1 (.D(multiplexer_1_out), .en(enable_i), .clk(clk_i), .Q(register_1_q), .clr(reset_i));
  Comparator #(.width(2)) comparator_1 (.a(register_1_q), .b(2'b01), .eq(out_o));  // open: gt, lt

  // Notes on the sheet:
  //   Attention, votre version de Logisim
  //   ne contient pas de tracker. Si vous
  //   enregistrez votre projet, toutes les
  //   informations du tracker seront
  //   définitivement effacées.
endmodule

module decodeur_sorties (
  input  [6:0] in_i,
  output [6:0] out_o
);

  wire [6:0] multiplexer_1_out, multiplexer_2_out, multiplexer_3_out, multiplexer_4_out, multiplexer_5_out,
       multiplexer_6_out, multiplexer_7_out;

  Multiplexer #(.width(7), .enable("false")) multiplexer_1 (
    .in0({7{1'b0}}), .in1({7{1'b0}}), .out(multiplexer_1_out), .sel(in_i[0]));
  Multiplexer #(.width(7), .enable("false")) multiplexer_2 (
    .in0({7{1'b0}}), .in1(7'b1000000), .out(multiplexer_2_out), .sel(in_i[1]));
  Multiplexer #(.width(7), .enable("false")) multiplexer_3 (
    .in0({7{1'b0}}), .in1(7'b0100000), .out(multiplexer_3_out), .sel(in_i[2]));
  Multiplexer #(.width(7), .enable("false")) multiplexer_4 (
    .in0({7{1'b0}}), .in1(7'b0010100), .out(multiplexer_4_out), .sel(in_i[3]));
  Multiplexer #(.width(7), .enable("false")) multiplexer_5 (
    .in0({7{1'b0}}), .in1(7'b0011000), .out(multiplexer_5_out), .sel(in_i[4]));
  Multiplexer #(.width(7), .enable("false")) multiplexer_6 (
    .in0({7{1'b0}}), .in1(7'b0000001), .out(multiplexer_6_out), .sel(in_i[5]));
  Multiplexer #(.width(7), .enable("false")) multiplexer_7 (
    .in0({7{1'b0}}), .in1(7'b0010010), .out(multiplexer_7_out), .sel(in_i[6]));
  assign out_o = multiplexer_1_out | multiplexer_2_out | multiplexer_3_out | multiplexer_4_out | multiplexer_5_out | multiplexer_6_out | multiplexer_7_out;  // OR_Gate or_1, 7 bits wide

  // Notes on the sheet:
  //   Attention, votre version de Logisim
  //   ne contient pas de tracker. Si vous
  //   enregistrez votre projet, toutes les
  //   informations du tracker seront
  //   définitivement effacées.
  //   Wait
  //   ScanColor
  //   Unknow
  //   Blue
  //   Red
  //   Drop
  //   ResetPos
endmodule

module decodeur_etats_futurs (
  input  [6:0] etat_actuel,
  input  ready_i,
  input  [1:0] color_i,
  input  clk_i,
  output [6:0] etat_futur
);

  wire and_1_out, and_2_out, and_3_out, and_4_out, and_6_out, and_7_out, and_8_out, and_9_out, and_10_out,
       and_11_out, and_12_out, not_1_out, not_2_out, not_3_out, not_4_out, not_5_out, not_6_out, not_7_out,
       not_8_out, timer, xnor_1_out;

  NotExactlyOne xnor_1 (.out(xnor_1_out), .in0(etat_actuel[3]), .in1(etat_actuel[2]), .in2(etat_actuel[0]));
  timer timer_1 (.load_i(xnor_1_out), .enable_i(1'b1), .clk_i(clk_i), .reset_i(1'b0), .out_o(timer));
  not not_1 (not_1_out, ready_i);
  not not_2 (not_2_out, color_i[0]);
  not not_3 (not_3_out, color_i[1]);
  not not_4 (not_4_out, color_i[1]);
  not not_5 (not_5_out, timer);
  not not_6 (not_6_out, color_i[0]);
  not not_7 (not_7_out, timer);
  not not_8 (not_8_out, timer);
  and and_1 (and_1_out, etat_actuel[6], not_1_out);
  and and_2 (and_2_out, etat_actuel[0], timer);
  and and_3 (and_3_out, etat_actuel[6], ready_i);
  and and_4 (and_4_out, etat_actuel[5], color_i[0], color_i[1]);
  and and_5 (etat_futur[4], etat_actuel[5], not_2_out, not_3_out);
  and and_6 (and_6_out, etat_actuel[5], color_i[0], not_4_out);
  and and_7 (and_7_out, etat_actuel[3], not_5_out);
  and and_8 (and_8_out, etat_actuel[5], not_6_out, color_i[1]);
  and and_9 (and_9_out, etat_actuel[2], not_7_out);
  and and_10 (and_10_out, timer, etat_actuel[3]);
  and and_11 (and_11_out, timer, etat_actuel[2]);
  and and_12 (and_12_out, not_8_out, etat_actuel[0]);
  or or_1 (etat_futur[6], and_1_out, etat_actuel[4], and_2_out);
  or or_2 (etat_futur[5], and_3_out, and_4_out);
  or or_3 (etat_futur[3], and_6_out, and_7_out);
  or or_4 (etat_futur[2], and_8_out, and_9_out);
  or or_5 (etat_futur[1], and_10_out, and_11_out);
  or or_6 (etat_futur[0], and_12_out, etat_actuel[1]);

  // Other names for the same wires on the sheet: color0 = color_i[0]; color1 = color_i[1]; ResetPos = etat_actuel[0];
  //   Drop = etat_actuel[1]; Red = etat_actuel[2]; Blue = etat_actuel[3]; Unknow = etat_actuel[4];
  //   ScanColor = etat_actuel[5]; Wait_ = etat_actuel[6]; ResetPosNext = etat_futur[0]; DropNext = etat_futur[1];
  //   RedNext = etat_futur[2]; BlueNext = etat_futur[3]; UnknowNext = etat_futur[4]; ScanColorNext = etat_futur[5];
  //   WaitNext = etat_futur[6]; ready = ready_i

  // Notes on the sheet:
  //   Attention, votre version de Logisim
  //   ne contient pas de tracker. Si vous
  //   enregistrez votre projet, toutes les
  //   informations du tracker seront
  //   définitivement effacées.
endmodule

module registre_7_bits (
  input  [6:0] in_i,
  input  reset_i,
  input  clk,
  output [6:0] out_o
);

  wire multiplexer_1_out, multiplexer_2_out, multiplexer_3_out, multiplexer_4_out, multiplexer_5_out,
       multiplexer_6_out, multiplexer_7_out, not_1_out;

  not not_1 (not_1_out, reset_i);
  D_Flip_Flop d_ff_1 (.D(multiplexer_1_out), .clk(clk), .Q(out_o[0]), .preset(reset_i));  // open: Qn, reset
  Multiplexer #(.enable("false")) multiplexer_1 (
    .in0(out_o[0]), .in1(in_i[0]), .out(multiplexer_1_out), .sel(not_1_out));
  D_Flip_Flop d_ff_2 (.D(multiplexer_2_out), .clk(clk), .Q(out_o[1]), .reset(reset_i));  // open: Qn, preset
  Multiplexer #(.enable("false")) multiplexer_2 (
    .in0(out_o[1]), .in1(in_i[1]), .out(multiplexer_2_out), .sel(not_1_out));
  D_Flip_Flop d_ff_3 (.D(multiplexer_3_out), .clk(clk), .Q(out_o[2]), .reset(reset_i));  // open: Qn, preset
  Multiplexer #(.enable("false")) multiplexer_3 (
    .in0(out_o[2]), .in1(in_i[2]), .out(multiplexer_3_out), .sel(not_1_out));
  D_Flip_Flop d_ff_4 (.D(multiplexer_4_out), .clk(clk), .Q(out_o[3]), .reset(reset_i));  // open: Qn, preset
  Multiplexer #(.enable("false")) multiplexer_4 (
    .in0(out_o[3]), .in1(in_i[3]), .out(multiplexer_4_out), .sel(not_1_out));
  D_Flip_Flop d_ff_5 (.D(multiplexer_5_out), .clk(clk), .Q(out_o[4]), .reset(reset_i));  // open: Qn, preset
  Multiplexer #(.enable("false")) multiplexer_5 (
    .in0(out_o[4]), .in1(in_i[4]), .out(multiplexer_5_out), .sel(not_1_out));
  D_Flip_Flop d_ff_6 (.D(multiplexer_6_out), .clk(clk), .Q(out_o[5]), .reset(reset_i));  // open: Qn, preset
  Multiplexer #(.enable("false")) multiplexer_6 (
    .in0(out_o[5]), .in1(in_i[5]), .out(multiplexer_6_out), .sel(not_1_out));
  D_Flip_Flop d_ff_7 (.D(multiplexer_7_out), .clk(clk), .Q(out_o[6]), .reset(reset_i));  // open: Qn, preset
  Multiplexer #(.enable("false")) multiplexer_7 (
    .in0(out_o[6]), .in1(in_i[6]), .out(multiplexer_7_out), .sel(not_1_out));

  // Notes on the sheet:
  //   Attention, votre version de Logisim
  //   ne contient pas de tracker. Si vous
  //   enregistrez votre projet, toutes les
  //   informations du tracker seront
  //   définitivement effacées.
endmodule
